# Fritzing sketch accelerometer-adxl345 (saved by Fritzing 0.9.0b)

parts:
  Part3 = Arduino Uno (Rev3)
  Part4 = Triple Axis Accelerometer Breakout - ADXL345

nets:
  N1: Part3.A4/SDA, Part4.SDA
  N2: Part3.A5/SCL, Part4.SCL
  5V: Part3.5V, Part4.VCC, Part4.CS
  GND: Part3.GND, Part4.GND

notes:
  Note the jumper across VCC and CS: this is required for SparkFun & RioRand versions. AdaFruit's does not require the jumper.
