# Fritzing sketch barometer-mpl3115a2 (saved by Fritzing 0.9.1b)

parts:
  Part2 = Arduino Uno (Rev3)
  Part3 = Altitude/Pressure Sensor - MPL3115A2 Breakout [part_number=SEN-11084]

nets:
  N1: Part2.A4/SDA, Part3.SDA
  N2: Part2.A5/SCL, Part3.SCL
  5V: Part2.5V, Part3.VCC
  GND: Part2.GND, Part3.GND
