# Fritzing sketch button-options (saved by Fritzing 0.8.7b)
breadboards: 1

parts:
  S1 = Pushbutton [package="[THT]"]
  R1 = Resistor [tolerance=±5% resistance=10k package=THT]
  Arduino3 = Arduino Uno (Rev3)

nets:
  N1: S1.Pin_1, S1.Pin_2, R1.Pin_0, Arduino3.D8
  N2: S1.Pin_3, S1.Pin_4
  N3: R1.Pin_1, Arduino3.GND

notes:
  button signal line
  10k OHM Resistor
