# Fritzing sketch directional-motor (saved by Fritzing 0.8.0b)
breadboards: 1

parts:
  Arduino1 = Arduino
  M1 = DC Motor
  Part1 = Arduino Motor Shield

nets:
  N1: Arduino1.GND, M1.pin_1
  N2: M1.pin_2, Part1.D3
