# Fritzing sketch hc-sr04 (saved by Fritzing 0.7.11b)
breadboards: 1

parts:
  Arduino1 = Arduino
  Part1 = SRF05 Ultrasonic Rangefinder

nets:
  GND: Arduino1.GND, Part1.GND
  N1: Arduino1.D7, Part1.Trig
  +5V: Arduino1.+5V, Part1.VCC
