# Fritzing sketch joystick-motor-led (saved by Fritzing 0.8.7b)
breadboards: 1

parts:
  M1 = DC Motor
  Part1 = Thumb Joystick
  LED1 = LED - 5mm [color="Red (633nm)" package="5 mm [THT]"]
  Arduino1 = Arduino Uno (Rev3)

nets:
  GND: M1.pin_1, Part1.GND, LED1.cathode, Arduino1.GND
  N1: M1.pin_2, Arduino1.D5_PWM
  N2: Part1.HORZ, Arduino1.A1
  N3: Part1.VERT, Arduino1.A0
  N4: LED1.anode, Arduino1.D13/SCK
