# Fritzing sketch joystick (saved by Fritzing 0.7.1b)
breadboards: 1

parts:
  Arduino1 = Arduino
  Part1 = Thumb Joystick

nets:
  +5V: Arduino1.+5V, Part1.VCC
  GND: Arduino1.GND, Part1.GND
  N1: Arduino1.A0, Part1.VERT
  N2: Arduino1.A1, Part1.HORZ
