# Fritzing sketch led-fade-callback (saved by Fritzing 0.8.7b)
breadboards: 1

parts:
  Part1 = Arduino Uno (Rev3)
  R1 = Resistor [tolerance=±5% resistance=220 package=THT]
  R2 = Resistor [tolerance=±5% resistance=220 package=THT]
  LED1 = LED - 5mm [color="Red (633nm)" package="5 mm [THT]"]
  LED2 = LED - 5mm [color="Red (633nm)" package="5 mm [THT]"]
  LED3 = LED - 5mm [color="Red (633nm)" package="5 mm [THT]"]
  R3 = Resistor [tolerance=±5% resistance=220 package=THT]
  LED4 = LED - 5mm [color="Red (633nm)" package="5 mm [THT]"]
  R4 = Resistor [tolerance=±5% resistance=220 package=THT]
  LED5 = LED - 5mm [color="Red (633nm)" package="5 mm [THT]"]
  R5 = Resistor [tolerance=±5% resistance=220 package=THT]
  LED6 = LED - 5mm [color="Red (633nm)" package="5 mm [THT]"]
  R6 = Resistor [tolerance=±5% resistance=220 package=THT]

nets:
  N1: Part1.D9_PWM, LED3.anode
  N2: Part1.D10_PWM/SS, LED2.anode
  N3: Part1.D11_PWM/MOSI, LED1.anode
  N4: Part1.D3_PWM, LED6.anode
  N5: Part1.D5_PWM, LED5.anode
  N6: Part1.D6_PWM, LED4.anode
  N7: Part1.GND, R1.Pin_0, R2.Pin_0, R3.Pin_0, R4.Pin_0, R5.Pin_0, R6.Pin_0
  N8: R1.Pin_1, LED1.cathode
  N9: R2.Pin_1, LED2.cathode
  N10: LED3.cathode, R3.Pin_1
  N11: LED4.cathode, R4.Pin_1
  N12: LED5.cathode, R5.Pin_1
  N13: LED6.cathode, R6.Pin_1
