# Fritzing sketch led-rainbow (saved by Fritzing 0.8.7b)
breadboards: 1

parts:
  Part1 = Arduino Uno (Rev3)
  LED4 = RGB LED (com. cathode, rgb) [package="5 mm [THT]"]

nets:
  N1: Part1.GND, LED4.common_cathode
  N2: Part1.D3_PWM, LED4.blue_anode
  N3: Part1.D5_PWM, LED4.green_anode
  N4: Part1.D6_PWM, LED4.red_anode
