# Fritzing sketch led-rgb-PCA9685 (saved by Fritzing 0.8.7b)
breadboards: 1

parts:
  Part1 = Arduino Uno (Rev3)
  PWM1 = PCA9685 16x12-bit PWM Breakout
  LED2 = RGB LED (com. cathode, rgb) [package="5 mm [THT]"]

nets:
  N1: Part1.A4/SDA, PWM1.no_name_yet#504
  N2: Part1.A5/SCL, PWM1.no_name_yet#503
  N3: Part1.5V, PWM1.no_name_yet#505
  N4: Part1.GND, PWM1.no_name_yet#501, PWM1.no_name_yet#1002, LED2.common_cathode
  N5: PWM1.no_name_yet#0, LED2.blue_anode
  N6: PWM1.no_name_yet#1, LED2.green_anode
  N7: PWM1.no_name_yet#2, LED2.red_anode
