# Fritzing sketch led-rgb-anode (saved by Fritzing 0.8.7b)
breadboards: 1

parts:
  Part1 = Arduino Uno (Rev3)
  R7 = Resistor [resistance=220 tolerance=±5% package=THT]
  R8 = Resistor [resistance=220 tolerance=±5% package=THT]
  R9 = Resistor [resistance=220 tolerance=±5% package=THT]
  LED1 = RGB LED - (4 legs) [package="5 mm [THT]"]

nets:
  N1: Part1.D3_PWM, R9.Pin_0
  N2: Part1.D5_PWM, R8.Pin_0
  N3: Part1.D6_PWM, R7.Pin_0
  N4: Part1.5V, LED1.common_anode
  N5: R7.Pin_1, LED1.blue_cathode
  N6: R8.Pin_1, LED1.green_cathode
  N7: R9.Pin_1, LED1.red_cathode
