# Fritzing sketch led-rgb (saved by Fritzing 0.9.1b)
breadboards: 1

parts:
  Part1 = Arduino Uno (Rev3)
  LED2 = RGB LED (com. anode, rbg) [package="5 mm [THT]"]

nets:
  N1: Part1.D9_PWM, LED2.green_cathode
  N2: Part1.D10_PWM/SS, LED2.common_anode
  N3: Part1.D11_PWM/MOSI, LED2.red_cathode
  N4: Part1.GND, LED2.blue_cathode
