# Fritzing sketch motor-directional (saved by Fritzing 0.7.12b)

parts:
  Arduino1 = Arduino  # not connected
  M1 = DC Motor
  Part1 = Arduino Motor Shield

nets:
  N1: M1.pin_1, Part1.OUT4
  N2: M1.pin_2, Part1.OUT3
