# Fritzing sketch multi-bmp180 (saved by Fritzing 0.9.1b)

parts:
  Part1 = Arduino Uno (Rev3)
  BMP1 = BMP180

nets:
  N1: Part1.A4/SDA, BMP1.SDA
  N2: Part1.A5/SCL, BMP1.SCL
  5V: Part1.5V, BMP1.VIN
  GND: Part1.GND, BMP1.GND
