# Fritzing sketch navigator-joystick (saved by Fritzing 0.8.7b)

parts:
  Part2 = Thumb Joystick
  J2 = Basic Servo
  LED2 = LED - 5mm [color="Red (633nm)" package="5 mm [THT]"]
  Arduino4 = Arduino Uno (Rev3)
  Arduino5 = Arduino Uno (Rev3)

nets:
  GND: Part2.GND, Arduino4.GND
  N1: Part2.HORZ, Arduino4.A1
  N2: Part2.VERT, Arduino4.A0
  GND_2: J2.gnd, LED2.cathode, Arduino5.GND
  N3: J2.pulse, Arduino5.D9_PWM
  N4: LED2.anode, Arduino5.D13/SCK

notes:
  navigator
  controller
