# Fritzing sketch potentiometer (saved by Fritzing 0.7.1b)
breadboards: 1

parts:
  R1 = Rotary Potentiometer (Large) [maximum_resistance=100kΩ package=THT]
  Arduino2 = Arduino

nets:
  N1: R1.leg1, Arduino2.GND
  N2: R1.wiper, Arduino2.A3
  N3: R1.leg2, Arduino2.+5V
