# Fritzing sketch sensor-slider (saved by Fritzing 0.8.7b)
breadboards: 1

parts:
  Arduino2 = Arduino Uno (Rev3)
  VCC1 = 4 x AAA Battery Mount
  U1 = SLIDER [package=slider]

nets:
  N1: Arduino2.A0, U1.E
  N2: Arduino2.GND, VCC1.-, U1.S
  N3: VCC1.+, U1.A
