# Fritzing sketch stepper-driver (saved by Fritzing 0.9.3b)
breadboards: 1

parts:
  DRV1 = A4983
  M1 = Stepper Motor - Bipolar
  C1 = Electrolytic Capacitor [capacitance=100µF voltage=35V package="200 mil [THT, electrolytic]"]
  Part1 = Arduino Uno (Rev3)

nets:
  VDD: DRV1.RST, DRV1.VDD, Part1.5V
  N1: DRV1.STEP, Part1.D12/MISO
  N2: DRV1.DIR, Part1.D11_PWM/MOSI
  N3: DRV1.VMOT, C1.+
  N4: DRV1.GNDMOT, C1.-
  N5: DRV1.2B, M1.A
  N6: DRV1.2A, M1.C
  N7: DRV1.1A, M1.B
  N8: DRV1.1B, M1.D
  GND: DRV1.GND, Part1.GND

notes:
  Motor Power

custom parts:
  A4983: Poloko A4983 Stepper Motor Control Breakout
