# Fritzing sketch temperature-HTU21D (saved by Fritzing 0.9.1b)

parts:
  Part3 = Arduino Uno (Rev3)
  Part4 = HTU21D Breakout

nets:
  N1: Part3.A4/SDA, Part4.SDA
  N2: Part3.A5/SCL, Part4.SCL
  5V: Part3.5V, Part4.3.3V
  GND: Part3.GND, Part4.GND

custom parts:
  HTU21D Breakout: This is a breadboard friendly breakout board for the Measurement Specialties high-precision, low-power digital humidity sensor.
