# Fritzing sketch toggle-switch (saved by Fritzing 0.8.7b)
breadboards: 1

parts:
  S1 = Toggle Switch [package=THT]
  R1 = Resistor [tolerance=±5% resistance=10k package=THT]
  Arduino1 = Arduino Uno (Rev3)

nets:
  N1: S1.L1, R1.Pin_1, Arduino1.D8
  N2: R1.Pin_0, Arduino1.GND
